// Logisim project another flipflop.circ as structural Verilog: 1 circuit, main circuit main
module main (
  input  y,
  input  z,
  output out
);

  wire and_1_out, clock_1_out;

  Clock clock_1 (.out(clock_1_out));
  and and_1 (and_1_out, out, y);
  J_K_Flip_Flop j_k_ff_1 (.J(and_1_out), .clk(clock_1_out), .K(z), .Q(out));  // open: Qn, preset, en, reset

  // Notes on the sheet:
  //   x
endmodule
