// Logisim project d flipflop.circ as structural Verilog: 2 circuits, main circuit main
module main (
  input  x,
  input  y,
  output sum,
  output q
);

  wire clock_1_out, fulladd_1_cout;

  fulladd fulladd_1 (.x(x), .y(y), .cin(q), .sum(sum), .cout(fulladd_1_cout));
  Clock clock_1 (.out(clock_1_out));
  D_Flip_Flop d_ff_1 (.clk(clock_1_out), .D(fulladd_1_cout), .Q(q));  // open: Qn, preset, en, reset
endmodule

module fulladd (
  input  x,
  input  y,
  input  cin,
  output sum,
  output cout
);

  wire and_1_out, and_2_out, xor_1_out;

  xor xor_1 (xor_1_out, x, y);
  and and_1 (and_1_out, y, x);
  xor xor_2 (sum, xor_1_out, cin);
  and and_2 (and_2_out, xor_1_out, cin);
  or or_1 (cout, and_2_out, and_1_out);
endmodule
